# Fritzing sketch circuit (saved by Fritzing 1.0.4)
breadboards: 1

parts:
  Bauteil1 = Arduino Nano (Rev3.0)
  DHT1 = DHT11 Humitidy and Temperature Sensor (3 pins)
  S1 = Pushbutton [package="[THT]"]
  S2 = Pushbutton [package="[THT]"]
  R1 = 10k Ω Resistor [package="0402 [SMD]"]
  R2 = 10k Ω Resistor [package="0402 [SMD]"]
  F1 = Fan - 4 wire [package=THT]
  OLED_I2C1 = OLED 128x64 I2C Monochrome Display
  JACK1 = 2.1mm Barrel Jack with Terminal Block
  U1 = Mini-360 DC-DC Buck converter [package=THT]

nets (from the schematic view):
  GND: Bauteil1.GND, DHT1.Gnd, R1.Pin_0, R2.Pin_0, OLED_I2C1.GND, U1.OUT-
  N1: Bauteil1.D2, DHT1.Plus
  N2: Bauteil1.D3, S2.Pin_1, S2.Pin_2, R1.Pin_1
  N3: Bauteil1.D4, S1.Pin_1, S1.Pin_2, R2.Pin_1
  N4: Bauteil1.D9, F1.Tach
  VIN: Bauteil1.VIN, DHT1.Signal, S1.Pin_3, S1.Pin_4, S2.Pin_3, S2.Pin_4, OLED_I2C1.VDD, U1.OUT+
  N5: Bauteil1.A5, OLED_I2C1.SDA
  N6: Bauteil1.A3, OLED_I2C1.SCK
  N7: F1.GND, JACK1.NEG, U1.IN-
  N8: F1.Power, JACK1.POS, U1.IN+

custom parts:
  DHT11 Humitidy and Temperature Sensor (3 pins): DHT11 Humidity and Temperature Sensor (3 pins).
  10k Ω Resistor: Resistor Basic schematic elements and footprints for 0603, 1206, and PTH resistors.
  Fan - 4 wire: Fan, 4 wire with tach.
  Mini-360 DC-DC Buck converter: Mini-360 DC-DC Buck converter. Tiny buck step down voltage converter, input voltage 4.75 to 23V output 1 to 17V adjustable. Available from ebay and the like.
